# Fritzing sketch ForSocketSketch (saved by Fritzing 1.0.2b)
breadboards: 1

parts:
  Компонент1 = node32s
  DHT1 = DHT11 Humitidy and Temperature Sensor
  R1 = Resistor [tolerance=±5% power=0.25W resistance=330 package=THT]
  LED1 = LED - 3mm [color="Yellow (592nm)" current=0.030A package="3 mm [THT]"]

nets:
  3.3V: Компонент1.3.3V, DHT1.VDD
  N1: Компонент1.V_BATT, DHT1.GND, LED1.anode
  N2: Компонент1.IO22, R1.Pin_0
  N3: Компонент1.IO21, DHT1.DATA
  N4: R1.Pin_1, LED1.cathode

custom parts:
  DHT11 Humitidy and Temperature Sensor: DHT11 Humidity and Temperature Sensor
